# Fritzing sketch fritzing (saved by Fritzing 0.9.3b)
circuit board: 8.46667cm x 5.64444cm

parts:
  LCD1602_I2C = LCD1602-I2C
  Part2 = Arduino Uno (Rev3)
  PMS5003_Sensor1 = Plantower PMS5003

nets:
  GND: LCD1602_I2C.GND, Part2.GND, PMS5003_Sensor1.GND
  VCC: LCD1602_I2C.VCC, Part2.5V, PMS5003_Sensor1.VCC
  N1: LCD1602_I2C.SDA, Part2.A4/SDA
  N2: LCD1602_I2C.SCL, Part2.A5/SCL
  N3: Part2.D0/RX, PMS5003_Sensor1.TXD
  N4: Part2.D1/TX, PMS5003_Sensor1.RXD

custom parts:
  LCD1602-I2C: A standard character display, usually with 2x16 characters. Comes in many colors with LCM1602 IIC attached.
  Plantower PMS5003: Particulate Matter Sensor
